// Logisim project processador.circ as structural Verilog: 5 circuits, main circuit main
module main (
  input  in_1,
  output [7:0] out_2,
  output [7:0] out_3
);

  wire and_1_out, Branch, clock_1_out, comp, Jump, li, not_1_out, or_2_out, or_3_out, RegWrit, soma,
       ula_1_igual, ula_1_maior, unidadecontrole_1_beq, unidadecontrole_1_bge, unidadecontrole_1_store,
       unidadecontrole_1_writereg;
  wire [2:0] functCtrl;
  wire [3:0] Opcode, R0, R1, R2;
  wire [7:0] adder_1_out, bit_extender_1_out, multiplexer_2_out, PC_q, ram_1_data, ula_1_r, WriteData;

  Register PC (.D(multiplexer_2_out), .Q(PC_q), .clk(clock_1_out), .clr(in_1));  // open: en
  Adder adder_1 (.a(8'h1), .b(PC_q), .out(adder_1_out));  // open: cin, cout
  ROM #(.dataWidth(16)) rom_1 (.addr(PC_q), .data({Opcode, R0, R1, R2}));  // open: sel
  Clock clock_1 (.out(clock_1_out));
  UnidadeControle unidadecontrole_1 (
    .a(Opcode[3]), .b(Opcode[2]), .c(Opcode[1]), .d(Opcode[0]), .Store(unidadecontrole_1_store),
    .WriteonRegorNot(RegWrit), .Soma(soma), .Writereg(unidadecontrole_1_writereg),
    .Beq(unidadecontrole_1_beq), .Bge(unidadecontrole_1_bge), .J(Jump), .Branch(Branch),
    .functCtrl1(functCtrl[0]), .functCtrl2(functCtrl[1]), .functCtrl3(functCtrl[2]), .Li(li));
  registradores Registradores (
    .Read_reg_1(R2), .Read_reg_2(R1), .Write_data(WriteData), .Write_reg(R0), .RegWrite(RegWrit),
    .CLOCK(clock_1_out), .CLEAR(1'b0), .Read_data_1(out_2), .Read_data_2(out_3));
  assign bit_extender_1_out = {{4{1'b0}}, R2};  // Bit_Extender bit_extender_1
  or or_1 (comp, unidadecontrole_1_beq, unidadecontrole_1_bge);
  not not_1 (not_1_out, clock_1_out);
  ULA ula_1 (
    .A(bit_extender_1_out), .B(out_3), .\Função (functCtrl), .Soma(soma), .Comp(comp), .R(ula_1_r),
    .maior(ula_1_maior), .Igual(ula_1_igual));  // open: Shamt
  RAM #(.bus("separate")) ram_1 (
    .addr(out_3), .din(out_2), .data(ram_1_data), .str(unidadecontrole_1_store), .sel(1'b1), .clk(not_1_out),
    .ld(1'b1));  // open: clr
  or or_2 (or_2_out, ula_1_maior, ula_1_igual);
  Multiplexer #(.width(8), .enable("false")) multiplexer_1 (
    .in0(ram_1_data), .in1(ula_1_r), .out(WriteData), .sel(unidadecontrole_1_writereg));
  or or_3 (or_3_out, Jump, and_1_out);
  and and_1 (and_1_out, or_2_out, Branch);
  Multiplexer #(.width(8), .enable("false")) multiplexer_2 (
    .in0(adder_1_out), .in1(bit_extender_1_out), .out(multiplexer_2_out), .sel(or_3_out));

  // Notes on the sheet:
  //   contents of rom_1 (hex, n*v repeats v):
  //   7300 2400 334 20f0 109 ff4 110c 22f0 4029 5020 110 ff4 6500
endmodule

module registradores (
  input  [3:0] Read_reg_1,
  input  [3:0] Read_reg_2,
  input  [7:0] Write_data,
  input  [3:0] Write_reg,
  input  RegWrite,
  input  CLOCK,
  input  CLEAR,
  output [7:0] Read_data_1,
  output [7:0] Read_data_2
);

  wire WE0, WE1, WE2, WE3, WE4, WE5, WE6, WE7;
  wire [7:0] demultiplexer_2_out0, demultiplexer_2_out1, demultiplexer_2_out2, demultiplexer_2_out3,
       demultiplexer_2_out4, demultiplexer_2_out5, demultiplexer_2_out6, demultiplexer_2_out7, Reg0, Reg1,
       Reg2, Reg3, Reg4, Reg5, Reg6, Reg7;

  Demultiplexer #(.select(4), .enable("false")) demultiplexer_1 (
    .out0(WE0), .out1(WE1), .out2(WE2), .out3(WE3), .out4(WE4), .out5(WE5), .out6(WE6), .out7(WE7),
    .in(RegWrite), .sel(Write_reg));  // open: out8, out9, out10, out11, out12, out13, out14, out15
  Demultiplexer #(.select(4), .width(8), .enable("false")) demultiplexer_2 (
    .out0(demultiplexer_2_out0), .out1(demultiplexer_2_out1), .out2(demultiplexer_2_out2),
    .out3(demultiplexer_2_out3), .out4(demultiplexer_2_out4), .out5(demultiplexer_2_out5),
    .out6(demultiplexer_2_out6), .out7(demultiplexer_2_out7), .in(Write_data), .sel(Write_reg));  // open: out8, out9, out10, out11, out12, out13, out14, out15
  Register Reg_0 (.D(demultiplexer_2_out0), .en(WE0), .Q(Reg0), .clk(CLOCK), .clr(CLEAR));
  Register Reg_1 (.D(demultiplexer_2_out1), .en(WE1), .Q(Reg1), .clk(CLOCK), .clr(CLEAR));
  Register Reg_2 (.D(demultiplexer_2_out2), .en(WE2), .Q(Reg2), .clk(CLOCK), .clr(CLEAR));
  Register Reg_3 (.D(demultiplexer_2_out3), .en(WE3), .Q(Reg3), .clk(CLOCK), .clr(CLEAR));
  Register Reg_4 (.D(demultiplexer_2_out4), .en(WE4), .Q(Reg4), .clk(CLOCK), .clr(CLEAR));
  Register Reg_5 (.D(demultiplexer_2_out5), .en(WE5), .Q(Reg5), .clk(CLOCK), .clr(CLEAR));
  Register Reg_6 (.D(demultiplexer_2_out6), .en(WE6), .Q(Reg6), .clk(CLOCK), .clr(CLEAR));
  Register Reg_7 (.D(demultiplexer_2_out7), .en(WE7), .Q(Reg7), .clk(CLOCK), .clr(CLEAR));
  Multiplexer #(.select(4), .width(8), .enable("false")) multiplexer_1 (
    .in0(Reg0), .in1(Reg1), .in2(Reg2), .in3(Reg3), .in4(Reg4), .in5(Reg5), .in6(Reg6), .in7(Reg7),
    .out(Read_data_1), .sel(Read_reg_1));  // open: in8, in9, in10, in11, in12, in13, in14, in15
  Multiplexer #(.select(4), .width(8), .enable("false")) multiplexer_2 (
    .in0(Reg0), .in1(Reg1), .in2(Reg2), .in3(Reg3), .in4(Reg4), .in5(Reg5), .in6(Reg6), .in7(Reg7),
    .out(Read_data_2), .sel(Read_reg_2));  // open: in8, in9, in10, in11, in12, in13, in14, in15

  // Other names for the same wires on the sheet: Read1[3:0] = Read_reg_1; Read2[3:0] = Read_reg_2
endmodule

module ULA (
  input  [7:0] A,
  input  [7:0] B,
  input  [2:0] \Função ,
  input  Soma,
  input  Comp,
  input  [2:0] Shamt,
  output [7:0] R,
  output maior,
  output Igual
);

  wire [7:0] AComp, adder_1_out, ADiv, AMult, ANeg, AShiftDir, AShiftEsq, ASoma, ASub, BComp, BDiv,
       bit_extender_1_out, bit_extender_2_out, BMult, BSoma, BSub, divider_1_out, multiplier_1_out,
       negator_1_out, shifter_1_out, shifter_2_out, subtractor_1_out;

  Demultiplexer #(.select(3), .width(8), .enable("false")) demultiplexer_1 (
    .out0(ASoma), .out1(ASub), .out2(AMult), .out3(ADiv), .out4(ANeg), .out5(AComp), .out6(AShiftEsq),
    .out7(AShiftDir), .in(A), .sel(\Função ));
  Demultiplexer #(.select(3), .width(8), .enable("false")) demultiplexer_2 (
    .out0(BSoma), .out1(BSub), .out2(BMult), .out3(BDiv), .out5(BComp), .in(B), .sel(\Função ));  // open: out4, out6, out7
  assign bit_extender_1_out = {{7{1'b0}}, Comp};  // Bit_Extender bit_extender_1
  Adder adder_1 (.a(ASoma), .b(BSoma), .out(adder_1_out));  // open: cin, cout
  Subtractor subtractor_1 (.a(ASub), .b(BSub), .out(subtractor_1_out));  // open: bin, bout
  Multiplier multiplier_1 (.a(AMult), .b(BMult), .out(multiplier_1_out));  // open: cin, cout
  Divider divider_1 (.a(ADiv), .b(BDiv), .out(divider_1_out));  // open: upper, rem
  Negator negator_1 (.in(ANeg), .out(negator_1_out));
  Comparator comparator_1 (.a(AComp), .b(BComp), .gt(maior), .eq(Igual));  // open: lt
  Shifter shifter_1 (.in(AShiftEsq), .\dist (Shamt), .out(shifter_1_out));
  Shifter #(.shift("lr")) shifter_2 (.in(AShiftDir), .\dist (Shamt), .out(shifter_2_out));
  assign bit_extender_2_out = {{7{1'b0}}, maior};  // Bit_Extender bit_extender_2
  Multiplexer #(.select(3), .width(8), .enable("false")) multiplexer_1 (
    .in0(adder_1_out), .in1(subtractor_1_out), .in2(multiplier_1_out), .in3(divider_1_out),
    .in4(negator_1_out), .in5(bit_extender_2_out), .in6(shifter_1_out), .in7(shifter_2_out), .out(R),
    .sel(\Função ));
endmodule

module UnidadeControle (
  input  a,
  input  b,
  input  c,
  input  d,
  output Store,
  output WriteonRegorNot,
  output Soma,
  output Writereg,
  output Beq,
  output Bge,
  output J,
  output Branch,
  output functCtrl1,
  output functCtrl2,
  output functCtrl3,
  output Li
);

  wire and_1_out, and_2_out, and_3_out, and_4_out, and_5_out, and_6_out, and_7_out, and_8_out, and_9_out,
       and_13_out, and_14_out, not_1_out, not_2_out, not_3_out, not_4_out, not_5_out, not_6_out, not_7_out,
       not_8_out, not_9_out, not_11_out, not_12_out, not_13_out, not_14_out, not_15_out, not_16_out,
       not_17_out, not_18_out, not_19_out, not_20_out, not_21_out, not_22_out, not_23_out, not_24_out,
       not_25_out, not_26_out;

  and and_1 (and_1_out, c, d);
  and and_2 (and_2_out, b, d);
  and and_3 (and_3_out, a, d);
  not not_1 (not_1_out, a);
  not not_2 (not_2_out, b);
  and and_4 (and_4_out, not_1_out, not_2_out, not_3_out);
  not not_3 (not_3_out, d);
  not not_4 (not_4_out, a);
  and and_5 (and_5_out, not_4_out, c, not_5_out);
  not not_5 (not_5_out, d);
  not not_6 (not_6_out, a);
  not not_7 (not_7_out, b);
  not not_8 (not_8_out, c);
  not not_9 (not_9_out, d);
  not not_10 (Writereg, c);
  not not_11 (not_11_out, a);
  not not_12 (not_12_out, b);
  not not_13 (not_13_out, c);
  not not_14 (not_14_out, a);
  not not_15 (not_15_out, c);
  not not_16 (not_16_out, d);
  not not_17 (not_17_out, a);
  not not_18 (not_18_out, b);
  not not_19 (not_19_out, c);
  not not_20 (not_20_out, a);
  not not_21 (not_21_out, c);
  not not_22 (not_22_out, d);
  and and_6 (and_6_out, b, not_23_out);
  not not_23 (not_23_out, c);
  and and_7 (and_7_out, a, b);
  and and_8 (and_8_out, b, not_24_out);
  not not_24 (not_24_out, c);
  and and_9 (and_9_out, a, b);
  not not_25 (not_25_out, a);
  not not_26 (not_26_out, d);
  or or_1 (Store, and_1_out, and_2_out, and_3_out);
  or or_2 (WriteonRegorNot, and_4_out, and_5_out);
  and and_10 (Soma, not_6_out, not_7_out, not_8_out, not_9_out);
  and and_11 (Beq, not_11_out, not_12_out, not_13_out, d);
  and and_12 (Bge, not_14_out, b, not_15_out, not_16_out);
  and and_13 (and_13_out, not_17_out, not_18_out, not_19_out, d);
  or or_3 (Branch, and_13_out, and_14_out);
  and and_14 (and_14_out, not_20_out, b, not_21_out, not_22_out);
  or or_4 (functCtrl1, d, and_6_out, and_7_out);
  or or_5 (functCtrl3, d, and_8_out, and_9_out);
  and and_15 (Li, not_25_out, b, c, not_26_out);

  assign functCtrl2 = 1'b0;
  assign J = 1'b0;
endmodule

module Controle_ULA (
  input  [2:0] funct,
  input  [1:0] ALUOp,
  output [2:0] ULACtrl
);

  Multiplexer #(.select(2), .width(3), .enable("false")) multiplexer_1 (
    .in0(3'b000), .in1(3'b101), .in2(funct), .in3(3'b000), .out(ULACtrl), .sel(ALUOp));
endmodule
